# Fritzing sketch HandBot (saved by Fritzing 0.9.3b)

parts:
  part = Basic Servo [part_number="Servo 3"]
  Часть1 = 16-Channel 12-bit PWM Servo Driver - I2C [part_number=815]
  Часть2 = Arduino Nano (Rev3.0)
  part_2 = Basic Servo [part_number="Servo 2"]
  part_3 = Basic Servo [part_number="Servo 1"]
  VCC1 = 4 x AAA Battery Mount
  S1 = SPST Switch [package=switch-spdt_kit]

nets:
  GND: part.gnd, Часть1.GND, Часть2.GND, part_2.gnd, part_3.gnd, S1.O
  VCC: part.vcc, Часть1.5.0V, part_2.vcc, part_3.vcc
  N1: part.pulse, Часть1.PWM10
  N2: Часть1.VCC, VCC1.+
  N3: Часть1.SDA, Часть2.A4
  N4: Часть1.SCL, Часть2.A5
  N5: Часть1.PWM9, part_2.pulse
  N6: Часть1.PWM8, part_3.pulse
  N7: VCC1.-, S1.P

custom parts:
  16-Channel 12-bit PWM Servo Driver - I2C: You want to make a cool robot, maybe a hexapod walker, or maybe just a piece of art with a lot of moving parts. Or maybe you want to drive a lot of LEDs with precise PWM output. Using only two pins, control 16 free-running PWM outputs! You can even chain up 62 breakouts to control up to 992 PWM outputs.
